# Fritzing sketch Throttle tester v010 (saved by Fritzing 0.8.0b)
breadboards: 1

parts:
  Arduino_Micro = Arduino Micro (Rev3)
  R1 = Rotary Potentiometer (Small)
  R2 = Resistor [tolerance=±5% resistance=10k package=THT]
  C1 = Electrolytic Capacitor [capacitance=1µF package="100 mil [THT, electrolytic]"]

nets:
  N1: Arduino_Micro.GND, R1.leg1, C1.-
  N2: Arduino_Micro.D10_PWM/A10, R2.Pin_1
  N3: Arduino_Micro.5V, R1.leg2
  N4: Arduino_Micro.A2, R2.Pin_0, C1.+
  N5: Arduino_Micro.A1, R1.wiper
